# Fritzing sketch Gr24_6487069_6487077 (saved by Fritzing 0.9.10b)
breadboards: 1

parts:
  U1 = 7-SEGMENT-4DIGIT [package=7-segment-4digit]
  BH1750FVI_Breakout1 = BH1750 (GY-302) Breakout Board [part_number=BH1750FVI]
  esp3 = ESP32 DevKitc V4
  LED1 = smd LED [color="White (4500K)" package="0805 [SMD]"]
  R1 = Resistor [tolerance=±5% power=0.25 resistance=220 package=THT]
  DHT1 = DHT22 Humidity and Temperature Sensor
  J1 = Basic Servo

nets:
  GND: U1.1, BH1750FVI_Breakout1.GND, esp3.GND, J1.gnd
  VCC: U1.2, BH1750FVI_Breakout1.VCC, esp3.3V3, DHT1.DATA, DHT1.NULL, J1.vcc
  N1: U1.3, esp3.IO5
  N2: U1.4, esp3.IO4
  N3: BH1750FVI_Breakout1.SCL, esp3.IO22#16
  N4: BH1750FVI_Breakout1.SDA, esp3.IO21#13
  N5: esp3.IO15, R1.Pin_0
  N6: esp3.IO18, J1.pulse
  N7: esp3.IO22#21, DHT1.VDD
  N8: esp3.IO21#24, DHT1.GND
  N9: LED1.anode, R1.Pin_1

notes:
  6487069 Neadnapa
  6487077 Natheera

custom parts:
  BH1750 (GY-302) Breakout Board: The ROHM Semiconductor BH1750FVI is a digital ambient light sensor for the I2C bus interface. The BH750FVI is able to detect a wide range of light intensities (1-65535 lux). The spectral range is similar to that of the human eye.
  ESP32 DevKitc V4: ESP32-DevKitC board with ESP32-WROOM-32 module. ESP32-DevKitC V4 is a small-sized ESP32-based development board produced by Espressif. Most of the pins on the ESP module are broken out to the pin headers on the board. The pins D0, D1, D2, D3, CMD and CLK are used internally for communication between ESP32 and SPI flash memory. They are grouped on both sides near the USB connector. Avoid using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
